# Fritzing sketch Piano (saved by Fritzing 1.0.0rc)
breadboards: 2

parts:
  A1 = Particle - Photon2  # not connected
  S1 = Pushbutton [package="[THT]"]
  S2 = Pushbutton [package="[THT]"]
  S3 = Pushbutton [package="[THT]"]
  S4 = Pushbutton [package="[THT]"]
  S5 = Pushbutton [package="[THT]"]
  S6 = Pushbutton [package="[THT]"]
  S7 = Pushbutton [package="[THT]"]
  S8 = Pushbutton [package="[THT]"]
  R1 = Resistor [tolerance=±5% power=0.25W resistance=10k package=THT]
  R2 = Resistor [tolerance=±5% power=0.25W resistance=10k package=THT]
  R3 = Resistor [tolerance=±5% power=0.25W resistance=10k package=THT]
  R4 = Resistor [tolerance=±5% power=0.25W resistance=10k package=THT]
  R5 = Resistor [tolerance=±5% power=0.25W resistance=10k package=THT]
  R6 = Resistor [tolerance=±5% power=0.25W resistance=10k package=THT]
  R7 = Resistor [tolerance=±5% power=0.25W resistance=10k package=THT]
  R8 = Resistor [tolerance=±5% power=0.25W resistance=10k package=THT]
  J1 = Basic Servo
  P2 = S1133 Si Photodiode [package="8mm Ceramic [THT]"]
  P3 = S1133 Si Photodiode [package="8mm Ceramic [THT]"]
  P4 = S1133 Si Photodiode [package="8mm Ceramic [THT]"]
  P5 = S1133 Si Photodiode [package="8mm Ceramic [THT]"]
  R9 = Resistor [tolerance=±5% power=0.25W resistance=220 package=THT]
  R10 = Resistor [tolerance=±5% power=0.25W resistance=220 package=THT]
  R11 = Resistor [tolerance=±5% power=0.25W resistance=220 package=THT]
  R12 = Resistor [tolerance=±5% power=0.25W resistance=220 package=THT]
  OLED_I2C1 = OLED 128x64 I2C Monochrome Display
  J2 = Piezo Speaker
  S10 = Pushbutton [package="[THT]"]
  R13 = Resistor [tolerance=±5% power=0.25W resistance=10k package=THT]
  LED1 = LED - 5mm [color="Green (570nm)" current=0.030A package="5 mm [THT]"]
  R14 = Resistor [tolerance=±5% power=0.25W resistance=220 package=THT]

nets:
  N1: S1.Pin_1, S1.Pin_2, R1.Pin_0
  VCC: S1.Pin_3, S1.Pin_4, S2.Pin_3, S2.Pin_4, S3.Pin_3, S3.Pin_4, S4.Pin_3, S4.Pin_4, S5.Pin_3, S5.Pin_4, S6.Pin_3, S6.Pin_4, S7.Pin_3, S7.Pin_4, S8.Pin_3, S8.Pin_4, J1.vcc, P2.cathode, P3.cathode, P4.cathode, P5.cathode, OLED_I2C1.VDD, S10.Pin_3, S10.Pin_4
  N2: S2.Pin_1, S2.Pin_2, R2.Pin_0
  N3: S3.Pin_1, S3.Pin_2, R3.Pin_0
  N4: S4.Pin_1, S4.Pin_2, R4.Pin_0
  N5: S5.Pin_1, S5.Pin_2, R5.Pin_0
  N6: S6.Pin_1, S6.Pin_2, R6.Pin_0
  N7: S7.Pin_1, S7.Pin_2, R7.Pin_0
  N8: S8.Pin_1, S8.Pin_2, R8.Pin_0
  GND: R1.Pin_1, R2.Pin_1, R3.Pin_1, R4.Pin_1, R5.Pin_1, R6.Pin_1, R7.Pin_1, R8.Pin_1, J1.gnd, P2.anode, P3.anode, P4.anode, P5.anode, R9.Pin_0, R9.Pin_1, R10.Pin_0, R10.Pin_1, R11.Pin_0, R11.Pin_1, R12.Pin_0, R12.Pin_1, OLED_I2C1.GND, J2.pin1, R13.Pin_0, R14.Pin_1
  N9: S10.Pin_1, S10.Pin_2, R13.Pin_1
  N10: LED1.cathode, R14.Pin_0

custom parts:
  Particle - Photon2: The Photon 2 is a microcontroller and Wi-Fi networking developed by particle. Features: 802.11a/b/g/n Wi-Fi, 2.4 GHz and 5 GHz Integrated PCB antenna Integrated U.FL connector for external antenna Integrated RF switch BLE 5 using same antenna as Wi-Fi Realtek RTL8721DM MCU ARM Cortex M33 CPU, 200 MHz 2048 KB (2 MB) user application maximum size 3072 KB (3 MB) of RAM available to user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
